// Logisim project Lab_1.circ as structural Verilog: 3 circuits, main circuit main
module main (
  input  AND,
  input  AND_2,
  input  NOR,
  input  OR,
  input  NOR_2,
  input  OR_2,
  input  NOT,
  input  XOR,
  input  XOR_2,
  input  XNOR,
  input  XNOR_2,
  output AND_3,
  output NOR_3,
  output OR_3,
  output NOT_2,
  output XOR_3,
  output XNOR_3
);

  wire AND_out, NOR_2_out, NOR_3_out, NOR_out, OR_2_out, OR_out, XNOR_2_out, XNOR_3_out, XNOR_4_out,
       XNOR_out, XOR_2_out, XOR_3_out, XOR_out;

  nand u_AND (AND_out, AND, AND_2);
  nand u_OR (OR_out, OR, OR);
  nand u_OR_2 (OR_2_out, OR_2, OR_2);
  nand u_XOR (XOR_out, XOR, XOR_2);
  nand u_XNOR (XNOR_out, XNOR, XNOR_2);
  nand u_NOT (NOT_2, NOT, NOT);
  nand u_XOR_2 (XOR_2_out, XOR, XOR_out);
  nand u_XOR_3 (XOR_3_out, XOR_out, XOR_2);
  nand u_XNOR_2 (XNOR_2_out, XNOR, XNOR_out);
  nand u_XNOR_3 (XNOR_3_out, XNOR_out, XNOR_2);
  nand u_AND_2 (AND_3, AND_out, AND_out);
  nand u_OR_3 (OR_3, OR_out, OR_2_out);
  nand XOR_4 (XOR_3, XOR_2_out, XOR_3_out);
  nand XNOR_4 (XNOR_4_out, XNOR_2_out, XNOR_3_out);
  nand XNOR_5 (XNOR_3, XNOR_4_out, XNOR_4_out);
  nand u_NOR (NOR_out, NOR, NOR);
  nand u_NOR_2 (NOR_2_out, NOR_2, NOR_2);
  nand u_NOR_3 (NOR_3_out, NOR_out, NOR_2_out);
  nand NOR_4 (NOR_3, NOR_3_out, NOR_3_out);
endmodule

module NOR (
  input  AND,
  input  AND_2,
  input  OR,
  input  OR_2,
  input  NOT,
  input  XOR,
  input  XOR_2,
  input  XNOR,
  input  XNOR_2,
  output AND_3,
  output OR_3,
  output NOT_2,
  output XOR_3,
  output XNOR_3
);

  wire AND_2_out, AND_out, OR_out, XNOR_2_out, XNOR_3_out, XNOR_out, XOR_2_out, XOR_3_out, XOR_4_out, XOR_out;

  nor u_AND (AND_out, AND, AND);
  nor u_AND_2 (AND_2_out, AND_2, AND_2);
  nor u_OR (OR_out, OR, OR_2);
  nor u_NOT (NOT_2, NOT, NOT);
  nor u_XOR (XOR_out, XOR, XOR_2);
  nor u_XNOR (XNOR_out, XNOR, XNOR_2);
  nor u_AND_3 (AND_3, AND_out, AND_2_out);
  nor u_OR_2 (OR_3, OR_out, OR_out);
  nor u_XOR_2 (XOR_2_out, XOR, XOR_out);
  nor u_XOR_3 (XOR_3_out, XOR_out, XOR_2);
  nor u_XNOR_2 (XNOR_2_out, XNOR, XNOR_out);
  nor u_XNOR_3 (XNOR_3_out, XNOR_out, XNOR_2);
  nor XOR_4 (XOR_4_out, XOR_2_out, XOR_3_out);
  nor XNOR_4 (XNOR_3, XNOR_2_out, XNOR_3_out);
  nor XOR_5 (XOR_3, XOR_4_out, XOR_4_out);
endmodule

module COMP (
  input  [7:0] in_1,
  input  in_2,
  output [7:0] out_3
);

  xor xor_1 (out_3[6], in_2, in_1[6]);
  xor xor_2 (out_3[7], in_2, in_1[7]);
  xor xor_3 (out_3[5], in_2, in_1[5]);
  xor xor_4 (out_3[4], in_2, in_1[4]);
  xor xor_5 (out_3[3], in_2, in_1[3]);
  xor xor_6 (out_3[2], in_2, in_1[2]);
  xor xor_7 (out_3[1], in_2, in_1[1]);
  xor xor_8 (out_3[0], in_2, in_1[0]);
endmodule
