// Logisim project Lab_2.circ as structural Verilog: 4 circuits, main circuit main
module main (
  input  [3:0] in_1,
  input  in_2,
  input  A3,
  input  A2,
  input  A1,
  input  A0,
  input  C,
  output out_8,
  output [3:0] out_9,
  output COUT,
  output Y3,
  output Y2,
  output Y1,
  output Y0
);

  wire and_3_out, and_4_out, and_5_out, and_6_out, and_7_out, and_8_out;

  and and_1 (out_8, in_1[3], and_3_out);
  and and_2 (COUT, A3, and_4_out);
  and and_3 (and_3_out, in_1[2], and_5_out);
  xor xor_1 (out_9[3], in_1[3], and_3_out);
  xor xor_2 (Y3, A3, and_4_out);
  and and_4 (and_4_out, A2, and_6_out);
  and and_5 (and_5_out, in_1[1], and_7_out);
  xor xor_3 (out_9[2], in_1[2], and_5_out);
  xor xor_4 (Y2, A2, and_6_out);
  and and_6 (and_6_out, A1, and_8_out);
  xor xor_5 (out_9[1], in_1[1], and_7_out);
  and and_7 (and_7_out, in_1[0], in_2);
  and and_8 (and_8_out, A0, C);
  xor xor_6 (Y1, A1, and_8_out);
  xor xor_7 (out_9[0], in_1[0], in_2);
  xor xor_8 (Y0, A0, C);
endmodule

module INCRE (
  input  A3,
  input  A2,
  input  A1,
  input  A0,
  input  C,
  output COUT,
  output Y3,
  output Y2,
  output Y1,
  output Y0
);

  wire and_2_out, and_3_out, and_4_out;

  and and_1 (COUT, A3, and_2_out);
  xor xor_1 (Y3, A3, and_2_out);
  and and_2 (and_2_out, A2, and_3_out);
  and and_3 (and_3_out, A1, and_4_out);
  xor xor_2 (Y2, A2, and_3_out);
  and and_4 (and_4_out, A0, C);
  xor xor_3 (Y1, A1, and_4_out);
  xor xor_4 (Y0, A0, C);
endmodule

module _12BIT (
  input  in_1,
  input  [3:0] in_2,
  input  [3:0] in_3,
  input  [3:0] in_4,
  output [3:0] out_5,
  output out_6,
  output [3:0] out_7,
  output [3:0] out_8
);

  wire incre_1_cout, incre_2_cout;

  INCRE incre_1 (
    .A3(in_2[3]), .A2(in_2[2]), .A1(in_2[1]), .A0(in_2[0]), .COUT(incre_1_cout), .C(in_1), .Y3(out_7[3]),
    .Y2(out_7[2]), .Y1(out_7[1]), .Y0(out_7[0]));
  INCRE incre_2 (
    .A3(in_3[3]), .A2(in_3[2]), .A1(in_3[1]), .A0(in_3[0]), .COUT(incre_2_cout), .C(incre_1_cout),
    .Y3(out_8[3]), .Y2(out_8[2]), .Y1(out_8[1]), .Y0(out_8[0]));
  INCRE incre_3 (
    .A3(in_4[3]), .A2(in_4[2]), .A1(in_4[1]), .A0(in_4[0]), .COUT(out_6), .C(incre_2_cout), .Y3(out_5[3]),
    .Y2(out_5[2]), .Y1(out_5[1]), .Y0(out_5[0]));
endmodule

module DECRE (
  input  A3,
  input  A2,
  input  A1,
  input  A0,
  input  C,
  output COUT,
  output Y3,
  output Y2,
  output Y1,
  output Y0
);

  wire or_2_out, or_3_out, or_4_out;

  or or_1 (COUT, A3, or_2_out);
  xnor xnor_1 (Y3, A3, or_2_out);
  or or_2 (or_2_out, A2, or_3_out);
  or or_3 (or_3_out, A1, or_4_out);
  xnor xnor_2 (Y2, A2, or_3_out);
  or or_4 (or_4_out, A0, C);
  xnor xnor_3 (Y1, A1, or_4_out);
  xnor xnor_4 (Y0, A0, C);
endmodule
