// Logisim project Lab_3.circ as structural Verilog: 3 circuits, main circuit main
module main (
  input  A3,
  input  A2,
  input  A1,
  input  A0,
  input  C,
  input  P,
  output COUT,
  output P_2,
  output Y3,
  output Y2,
  output Y1,
  output Y0
);

  wire and_1_out, and_2_out, and_3_out, and_4_out, or_2_out, or_3_out, or_4_out;

  or or_1 (COUT, A3, or_2_out);
  xor xor_1 (Y3, A3, and_1_out);
  or or_2 (or_2_out, A2, or_3_out);
  and and_1 (and_1_out, or_2_out, P);
  xor xor_2 (Y2, A2, and_2_out);
  or or_3 (or_3_out, A1, or_4_out);
  and and_2 (and_2_out, or_3_out, P);
  and and_3 (and_3_out, or_4_out, P);
  xor xor_3 (Y1, A1, and_3_out);
  or or_4 (or_4_out, A0, C);
  xor xor_4 (Y0, A0, and_4_out);
  and and_4 (and_4_out, C, P);

  assign P_2 = P;
endmodule

module _1_S_2_S (
  input  [3:0] in_1,
  input  in_2,
  output [3:0] out_3
);

  wire or_1_out, or_2_out, or_3_out;

  xor xor_1 (out_3[3], in_1[3], or_1_out);
  or or_1 (or_1_out, in_1[2], or_2_out);
  or or_2 (or_2_out, in_1[1], or_3_out);
  xor xor_2 (out_3[2], in_1[2], or_2_out);
  xor xor_3 (out_3[1], in_1[1], or_3_out);
  or or_3 (or_3_out, in_1[0], in_2);
  xor xor_4 (out_3[0], in_1[0], in_2);
endmodule

module Controllef (
  input  [3:0] in_1,
  input  in_2,
  input  in_3,
  output [3:0] out_4
);

  wire and_1_out, and_2_out, and_3_out, xor_2_out, xor_4_out, xor_6_out;

  xor xor_1 (out_4[3], in_1[3], and_1_out);
  xor xor_2 (xor_2_out, in_1[2], in_2);
  and and_1 (and_1_out, xor_2_out, and_2_out);
  xor xor_3 (out_4[2], in_1[2], and_2_out);
  and and_2 (and_2_out, xor_4_out, and_3_out);
  xor xor_4 (xor_4_out, in_1[1], in_2);
  xor xor_5 (out_4[1], in_1[1], and_3_out);
  and and_3 (and_3_out, xor_6_out, in_3);
  xor xor_6 (xor_6_out, in_1[0], in_2);
  xor xor_7 (out_4[0], in_2, in_1[0]);
endmodule
