// Logisim project Lab_4.circ as structural Verilog
module BCD (
  input  a,
  input  b,
  input  c,
  input  d,
  output a_2,
  output b_2,
  output c_2,
  output d_2,
  output e,
  output f,
  output g
);

  wire and_1_out, and_2_out, and_3_out, and_4_out, and_5_out, and_6_out, and_7_out, and_8_out, and_9_out,
       and_10_out, and_11_out, and_12_out, and_13_out, and_14_out, and_15_out, and_16_out, and_17_out,
       not_1_out, not_2_out, not_3_out, not_4_out, not_5_out, not_6_out, not_7_out, not_8_out, not_9_out,
       not_10_out, not_11_out, not_12_out, not_13_out, not_14_out, not_15_out, not_16_out, not_17_out,
       not_18_out, not_19_out, not_20_out, not_21_out, not_22_out;

  not not_1 (not_1_out, a);
  and and_1 (and_1_out, not_1_out, not_2_out, not_3_out);
  not not_2 (not_2_out, b);
  not not_3 (not_3_out, d);
  and and_2 (and_2_out, b, d);
  and and_3 (and_3_out, a, d);
  not not_4 (not_4_out, b);
  not not_5 (not_5_out, c);
  and and_4 (and_4_out, not_5_out, not_6_out);
  not not_6 (not_6_out, d);
  and and_5 (and_5_out, c, d);
  not not_7 (not_7_out, c);
  or or_1 (c_2, not_7_out, d, b);
  not not_8 (not_8_out, b);
  and and_6 (and_6_out, not_8_out, not_9_out);
  not not_9 (not_9_out, d);
  not not_10 (not_10_out, b);
  and and_7 (and_7_out, not_10_out, c);
  and and_8 (and_8_out, c, not_11_out);
  not not_11 (not_11_out, d);
  not not_12 (not_12_out, c);
  and and_9 (and_9_out, b, not_12_out, d);
  not not_13 (not_13_out, b);
  and and_10 (and_10_out, not_13_out, not_14_out);
  not not_14 (not_14_out, d);
  and and_11 (and_11_out, c, not_15_out);
  not not_15 (not_15_out, d);
  not not_16 (not_16_out, c);
  and and_12 (and_12_out, not_16_out, not_17_out);
  not not_17 (not_17_out, d);
  and and_13 (and_13_out, b, not_18_out);
  not not_18 (not_18_out, c);
  and and_14 (and_14_out, b, not_19_out);
  not not_19 (not_19_out, d);
  not not_20 (not_20_out, b);
  and and_15 (and_15_out, not_20_out, c);
  and and_16 (and_16_out, b, not_21_out);
  not not_21 (not_21_out, c);
  and and_17 (and_17_out, b, not_22_out);
  not not_22 (not_22_out, d);
  or or_2 (a_2, and_1_out, c, and_2_out, and_3_out);
  or or_3 (b_2, not_4_out, and_4_out, and_5_out);
  or or_4 (d_2, and_6_out, and_7_out, and_8_out, and_9_out, a);
  or or_5 (e, and_10_out, and_11_out);
  or or_6 (f, and_12_out, and_13_out, and_14_out, a);
  or or_7 (g, and_15_out, and_16_out, and_17_out, a);
endmodule

module ROLL_NUM (
  input  a,
  input  b,
  input  c,
  input  d,
  output x3,
  output x2,
  output x1,
  output x0
);

  wire and_2_out, and_3_out, and_4_out, and_5_out, not_1_out, not_2_out, not_3_out, not_4_out, not_5_out,
       not_6_out;

  and and_1 (x3, b, not_1_out);
  not not_1 (not_1_out, c);
  not not_2 (not_2_out, a);
  not not_3 (not_3_out, b);
  and and_2 (and_2_out, not_2_out, not_3_out, not_4_out);
  not not_4 (not_4_out, d);
  and and_3 (and_3_out, b, c);
  not not_5 (not_5_out, b);
  and and_4 (and_4_out, not_5_out, c, d);
  and and_5 (and_5_out, b, not_6_out, d);
  not not_6 (not_6_out, c);
  or or_1 (x1, and_2_out, and_3_out);
  or or_2 (x0, and_4_out, and_5_out);

  assign x2 = a;
endmodule

module _7_SEGMENT (
  input  [3:0] in_1
);

  wire bcd_1_a_2, bcd_1_b_2, bcd_1_c_2, bcd_1_d_2, bcd_1_e, bcd_1_f, bcd_1_g, roll_num_1_x0, roll_num_1_x1,
       roll_num_1_x2, roll_num_1_x3;

  ROLL_NUM roll_num_1 (
    .a(in_1[3]), .b(in_1[2]), .c(in_1[1]), .d(in_1[0]), .x3(roll_num_1_x3), .x2(roll_num_1_x2),
    .x1(roll_num_1_x1), .x0(roll_num_1_x0));
  BCD bcd_1 (
    .a(roll_num_1_x0), .b(roll_num_1_x1), .c(roll_num_1_x2), .d(roll_num_1_x3), .a_2(bcd_1_a_2),
    .b_2(bcd_1_b_2), .c_2(bcd_1_c_2), .d_2(bcd_1_d_2), .e(bcd_1_e), .f(bcd_1_f), .g(bcd_1_g));
  _7_Segment_Display u_7_segment_display_1 (
    .g(bcd_1_g), .f(bcd_1_f), .a(bcd_1_a_2), .b(bcd_1_b_2), .e(bcd_1_e), .d(bcd_1_d_2), .c(bcd_1_c_2));  // open: dp
endmodule
