// Logisim project Lab_5.circ as structural Verilog: 2 circuits, main circuit main
module main (
  input  [3:0] A,
  input  [3:0] B,
  output EQ,
  output GT,
  output LT
);

  wire and_2_out, and_3_out, and_4_out, and_5_out, and_6_out, and_7_out, and_8_out, and_9_out, not_1_out,
       not_2_out, not_3_out, not_5_out, not_6_out, not_7_out, not_8_out, xnor_1_out, xnor_2_out, xnor_3_out,
       xnor_4_out;

  not not_1 (not_1_out, A[3]);
  not not_2 (not_2_out, A[2]);
  not not_3 (not_3_out, A[1]);
  not not_4 (not_3_out, A[0]);
  xnor xnor_1 (xnor_1_out, A[3], B[3]);
  xnor xnor_2 (xnor_2_out, A[2], B[2]);
  xnor xnor_3 (xnor_3_out, A[1], B[1]);
  and and_1 (EQ, xnor_1_out, xnor_2_out, xnor_3_out, xnor_4_out);
  xnor xnor_4 (xnor_4_out, A[0], B[0]);
  not not_5 (not_5_out, B[3]);
  not not_6 (not_6_out, B[2]);
  not not_7 (not_7_out, B[1]);
  not not_8 (not_8_out, B[0]);
  and and_2 (and_2_out, A[3], not_5_out);
  and and_3 (and_3_out, xnor_1_out, A[2], not_6_out);
  or or_1 (GT, and_2_out, and_3_out, and_4_out, and_5_out);
  and and_4 (and_4_out, xnor_1_out, xnor_2_out, A[1], not_7_out);
  and and_5 (and_5_out, xnor_2_out, xnor_1_out, xnor_4_out, not_8_out, A[0]);
  and and_6 (and_6_out, B[3], not_1_out);
  and and_7 (and_7_out, xnor_1_out, B[2], not_2_out);
  or or_2 (LT, and_6_out, and_7_out, and_8_out, and_9_out);
  and and_8 (and_8_out, xnor_2_out, xnor_1_out, B[1], not_3_out);
  and and_9 (and_9_out, xnor_2_out, xnor_1_out, xnor_4_out, B[0], not_5_out);
endmodule

module MIN_MAX (
  input  [3:0] A,
  input  [3:0] B,
  output [3:0] out_3,
  output [3:0] out_4
);

  wire main_1_gt, main_1_lt;

  main main_1 (.A(A), .B(B), .GT(main_1_gt), .LT(main_1_lt));  // open: EQ
  Multiplexer #(.width(4)) multiplexer_1 (.in0(B), .in1(A), .out(out_3), .sel(main_1_lt));  // open: en
  Multiplexer #(.width(4)) multiplexer_2 (.in0(B), .in1(A), .out(out_4), .sel(main_1_gt));  // open: en
endmodule
